# Fritzing sketch Esquema_Braco_Robotico (saved by Fritzing 0.9.10b)
breadboards: 1

parts:
  Componente1 = Arduino Uno (Rev3)
  Componente2 = Thumb Joystick

nets:
  N1: Componente1.A0, Componente2.HORZ
  N2: Componente1.A1, Componente2.VERT
  5V: Componente1.5V, Componente2.VCC
  GND: Componente1.GND, Componente2.GND
